# Fritzing sketch D1MINI_PC_CONTROL (saved by Fritzing 0.9.4)
circuit board: 5.46427cm x 4.17462cm
breadboards: 1

parts:
  WeMos_D1_Mini = WeMos D1 Mini
  Case = double row male pin header, 8 pins [form="♂ (male)"]
  Mother = double row male pin header, 8 pins [form="♂ (male)"]
  20k = Resistor [tolerance=±5% resistance=20k package=THT]
  20k_2 = Resistor [tolerance=±5% resistance=20k package=THT]
  20k_3 = Resistor [tolerance=±5% resistance=20k package=THT]
  20k_4 = Resistor [tolerance=±5% resistance=20k package=THT]
  100uF = Capacitor Polarized [part_number=100uF package=cpol-radial-100uf-25v]
  1k = Resistor [tolerance=±5% resistance=1k package=THT]
  15k = Resistor [tolerance=±5% resistance=15k package=THT]
  2N3904 = NPN-Transistor [part_number=2N3904 package="TO92 [THT]"]

nets:
  3.3V: WeMos_D1_Mini.3V3, 100uF.+
  PLED+: WeMos_D1_Mini.D0, Case.pin8, Mother.pin8, 20k_2.Pin_0
  LED_EN: WeMos_D1_Mini.D5, 1k.Pin_0, 15k.Pin_0
  RSW+: WeMos_D1_Mini.D6, Case.pin3, Mother.pin3, 20k_3.Pin_0
  PSW+: WeMos_D1_Mini.D7, Case.pin6, Mother.pin6, 20k_4.Pin_0
  HLED+: WeMos_D1_Mini.D8, Case.pin1, Mother.pin1, 20k.Pin_0
  GND: WeMos_D1_Mini.G, Case.pin4, Case.pin5, Mother.pin2, Mother.pin4, Mother.pin5, Mother.pin7, 20k.Pin_1, 20k_2.Pin_1, 20k_3.Pin_1, 20k_4.Pin_1, 100uF.-, 1k.Pin_1, 2N3904.E
  CHLED-/CPLED-: Case.pin2, Case.pin7, 2N3904.C
  N1: 15k.Pin_1, 2N3904.B
